# Fritzing sketch Assignment_2 (saved by Fritzing 0.9.3b)
breadboards: 1

parts:
  Part1 = Arduino Leonardo (Rev3b)
  R1 = Resistor [tolerance=±5% resistance=220 package=THT]
  LED1 = LED - 5mm [color="Green (565nm)" package="5 mm [THT]"]
  S1 = Pushbutton [package="[THT]"]
  R2 = Resistor [tolerance=±5% resistance=220 package=THT]

nets (from the breadboard view):
  N1: Part1.D7, S1.Pin_3, S1.Pin_4, R2.Pin_0
  N2: Part1.5V, S1.Pin_1, S1.Pin_2
  N3: Part1.GND, LED1.cathode, R2.Pin_1
  N4: Part1.D9_PWM/A9, R1.Pin_0
  N5: R1.Pin_1, LED1.anode
