# Fritzing sketch FinalProject (saved by Fritzing 0.9.3b)
breadboards: 1

parts:
  Part1 = Arduino Uno (Rev3)
  Power_plug1 = Power plug
  Resistor = NPN-Transistor [package="TO92 [THT]"]
  R1 = Resistor [tolerance=±5% resistance=10k package=THT]
  Part2 = Breakout Board for Electret Microphone
  IR_Receiver = IR Receiver Breakout [package=PCB]
  LED_Strip = smd LED [color="White (6500K)" package="0603 [SMD]"]

nets:
  N1: Part1.A0, Part2.AUD
  N2: Part1.D9_PWM, R1.Pin_0
  N3: Part1.D11_PWM/MOSI, IR_Receiver.OUT
  GND: Part1.GND, Power_plug1.GND, Resistor.E, Part2.GND, IR_Receiver.GND
  VCC: Part1.3V3, Part2.VCC, IR_Receiver.VCC
  N4: Power_plug1.VCC, LED_Strip.anode
  N5: Resistor.B, R1.Pin_1
  N6: Resistor.C, LED_Strip.cathode
