# Fritzing sketch Assignment3 (saved by Fritzing 0.9.3b)
breadboards: 1

parts:
  Arduino = Arduino Leonardo (Rev3b)
  R1 = Resistor [tolerance=±5% resistance=220 package=THT]
  LED1 = LED - 5mm [color="White (6500K)" package="5 mm [THT]"]
  R2 = Resistor [tolerance=±5% resistance=220 package=THT]
  LED2 = LED - 5mm [color="White (6500K)" package="5 mm [THT]"]
  Photo-resistor = Photocell (LDR) [package=THT]
  R4 = Resistor [tolerance=±5% resistance=10k package=THT]

nets (from the breadboard view):
  N1: Arduino.5V, Arduino.A0, Photo-resistor.pin_0
  N2: Arduino.GND, LED1.cathode, LED2.cathode, R4.Pin_1
  N3: Arduino.D9_PWM/A9, R1.Pin_0
  N4: Arduino.D10_PWM/A10, R2.Pin_0
  N5: R1.Pin_1, LED1.anode
  N6: R2.Pin_1, LED2.anode
  N7: Photo-resistor.pin_1, R4.Pin_0
