# Fritzing sketch Motor (saved by Fritzing 0.9.3b)
breadboards: 1

parts:
  Arduino = Arduino Uno (Rev3)
  Servo_motor = Basic Servo
  Joystick = Triple Axis Accelerometer Breakout - ADXL335

nets:
  N1: Arduino.A0, Joystick.XOUT
  N2: Arduino.A1, Joystick.YOUT
  N3: Arduino.D9_PWM, Servo_motor.pulse
  VCC: Arduino.5V, Servo_motor.vcc, Joystick.VCC
  GND: Arduino.GND, Servo_motor.gnd, Joystick.GND
