# Fritzing sketch assignment6 (saved by Fritzing 0.9.3b)
breadboards: 1

parts:
  Micro_Controller = Arduino Uno (Rev3)
  Rotary_potentiometer = Rotary Potentiometer (Small) [maximum_resistance=10kΩ package=THT]
  R2 = Resistor [tolerance=±5% resistance=10k package=THT]
  R3 = Resistor [tolerance=±5% resistance=10k package=THT]

nets:
  N1: Micro_Controller.A1, R2.Pin_0
  N2: Micro_Controller.5V, Rotary_potentiometer.leg1
  N3: Micro_Controller.GND, R3.Pin_1
  N4: Rotary_potentiometer.wiper, R2.Pin_1
  N5: Rotary_potentiometer.leg2, R3.Pin_0
