# Fritzing sketch transistor (saved by Fritzing 0.9.3b)
breadboards: 1

parts:
  Arduino = Arduino Uno (Rev3)
  R1 = Resistor [tolerance=±5% resistance=10k package=THT]
  12V_Power_Plug = Power plug
  LED_Strip = LED - 5mm [color="White (4500K)" package="5 mm [THT]"]
  Transistor = NPN-Transistor [package="TO92 [THT]"]
  R2 = Resistor [tolerance=±5% resistance=10k package=THT]
  Potentiometer = Rotary Potentiometer (Small) [maximum_resistance=10kΩ package=THT]

nets (from the schematic view):
  N1: Arduino.A0, R1.Pin_0, Potentiometer.wiper
  N2: Arduino.D9_PWM, R2.Pin_1
  GND: Arduino.GND, R1.Pin_1, 12V_Power_Plug.GND, Transistor.E
  N3: Arduino.5V, Potentiometer.leg1
  N4: 12V_Power_Plug.VCC, LED_Strip.anode
  N5: LED_Strip.cathode, Transistor.C
  N6: Transistor.B, R2.Pin_0
